# Fritzing sketch balancing robot (saved by Fritzing 0.9.4)
breadboards: 1

parts:
  Part1 = Arduino Nano (Rev3.0)  # not connected
  MD03A1 = Dual VNH2SP30 Motor Driver [part_number=MD03A]
  VCC1 = LC-R121R3P
  DC_Mot_Enc1 = DC Motor with two-phase hall-encoder [part_number=VT-E-G25A-06-177E]
  DC_Mot_Enc2 = DC Motor with two-phase hall-encoder [part_number=VT-E-G25A-06-177E]
  F1 = FUSE [package=fuse_5mm]
  S1 = Toggle Switch [package=THT]

nets:
  N1: MD03A1.OUT_1A, DC_Mot_Enc1.pin1
  N2: MD03A1.OUT_1B, DC_Mot_Enc1.pin2
  N3: MD03A1.OUT_2A, DC_Mot_Enc2.pin1
  N4: MD03A1.OUT_2B, DC_Mot_Enc2.pin2
  N5: MD03A1.VIN, F1.2
  N6: MD03A1.GND, VCC1.pin2
  N7: VCC1.pin1, S1.L1
  N8: F1.1, S1.COM

custom parts:
  LC-R121R3P: 12V 1.Ah battery
